// Logisim project F3-2to4-decoder.circ as structural Verilog: 20 circuits, main circuit decoder38
module decoder38 (
  input  in_1,
  input  in_2,
  input  in_3,
  output out_4,
  output out_5,
  output out_6,
  output out_7,
  output out_8,
  output out_9,
  output out_10,
  output out_11
);

  wire transistor_1_out;

  Transistor transistor_1 (.in(1'b1), .out(transistor_1_out), .gate(in_3));
  Transistor #(.\type ("n")) transistor_2 (.in(1'b0), .out(transistor_1_out), .gate(in_3));
  decoder24 decoder24_1 (._1(in_1), ._2(in_2), .en(transistor_1_out), .Y0(out_4), .Y1(out_5), .Y2(out_6), .Y3(out_7));
  decoder24 decoder24_2 (._1(in_1), ._2(in_2), .en(in_3), .Y0(out_8), .Y1(out_9), .Y2(out_10), .Y3(out_11));
endmodule

module OR2 (
  input  A,
  input  B,
  output Y
);

  wire transistor_1_out, transistor_2_out;

  Transistor transistor_1 (.in(1'b1), .out(transistor_1_out), .gate(A));
  Transistor transistor_2 (.in(transistor_1_out), .out(transistor_2_out), .gate(B));
  Transistor #(.\type ("n")) transistor_3 (.in(1'b0), .out(transistor_2_out), .gate(A));
  Transistor #(.\type ("n")) transistor_4 (.in(1'b0), .out(transistor_2_out), .gate(B));
  Transistor transistor_5 (.in(1'b1), .out(Y), .gate(transistor_2_out));
  Transistor #(.\type ("n")) transistor_6 (.in(1'b0), .out(Y), .gate(transistor_2_out));
endmodule

module decoder24 (
  input  _1,
  input  _2,
  input  en,
  output Y0,
  output Y1,
  output Y2,
  output Y3
);

  wire transistor_1_out, transistor_3_out, transistor_5_out, transistor_6_out, transistor_7_out,
       transistor_8_out, transistor_11_out, transistor_12_out, transistor_15_out, transistor_16_out,
       transistor_19_out, transistor_20_out, transistor_21_out, transistor_26_out;

  Transistor transistor_1 (.in(1'b1), .out(transistor_1_out), .gate(_1));
  Transistor #(.\type ("n")) transistor_2 (.in(1'b0), .out(transistor_1_out), .gate(_1));
  Transistor transistor_3 (.in(1'b1), .out(transistor_3_out), .gate(_2));
  Transistor #(.\type ("n")) transistor_4 (.in(1'b0), .out(transistor_3_out), .gate(_2));
  Transistor transistor_5 (.in(1'b1), .out(transistor_5_out), .gate(transistor_1_out));
  Transistor transistor_6 (.in(1'b1), .out(transistor_6_out), .gate(_1));
  Transistor #(.\type ("n")) transistor_7 (.in(1'b0), .out(transistor_7_out), .gate(en));
  Transistor #(.\type ("n")) transistor_8 (.in(transistor_7_out), .out(transistor_8_out), .gate(transistor_1_out));
  Transistor #(.\type ("n")) transistor_9 (.in(transistor_8_out), .out(transistor_5_out), .gate(transistor_3_out));
  Transistor transistor_10 (.in(1'b1), .out(transistor_5_out), .gate(en));
  Transistor #(.\type ("n")) transistor_11 (.in(1'b0), .out(transistor_11_out), .gate(en));
  Transistor #(.\type ("n")) transistor_12 (.in(transistor_11_out), .out(transistor_12_out), .gate(_1));
  Transistor #(.\type ("n")) transistor_13 (.in(transistor_12_out), .out(transistor_6_out), .gate(transistor_3_out));
  Transistor transistor_14 (.in(1'b1), .out(transistor_6_out), .gate(en));
  Transistor #(.\type ("n")) transistor_15 (.in(transistor_26_out), .out(transistor_15_out), .gate(transistor_1_out));
  Transistor #(.\type ("n")) transistor_16 (.in(transistor_15_out), .out(transistor_16_out), .gate(_2));
  Transistor transistor_17 (.in(1'b1), .out(transistor_16_out), .gate(en));
  Transistor transistor_18 (.in(1'b1), .out(transistor_16_out), .gate(transistor_1_out));
  Transistor #(.\type ("n")) transistor_19 (.in(1'b0), .out(transistor_19_out), .gate(en));
  Transistor #(.\type ("n")) transistor_20 (.in(transistor_19_out), .out(transistor_20_out), .gate(_1));
  Transistor #(.\type ("n")) transistor_21 (.in(transistor_20_out), .out(transistor_21_out), .gate(_2));
  Transistor transistor_22 (.in(1'b1), .out(transistor_21_out), .gate(en));
  Transistor transistor_23 (.in(1'b1), .out(transistor_21_out), .gate(_1));
  Transistor transistor_24 (.in(1'b1), .out(transistor_5_out), .gate(transistor_3_out));
  Transistor transistor_25 (.in(1'b1), .out(transistor_6_out), .gate(transistor_3_out));
  Transistor #(.\type ("n")) transistor_26 (.in(1'b0), .out(transistor_26_out), .gate(en));
  Transistor transistor_27 (.in(1'b1), .out(transistor_16_out), .gate(_2));
  Transistor transistor_28 (.in(1'b1), .out(transistor_21_out), .gate(_2));
  Transistor transistor_29 (.in(1'b1), .out(Y0), .gate(transistor_5_out));
  Transistor #(.\type ("n")) transistor_30 (.in(1'b0), .out(Y0), .gate(transistor_5_out));
  Transistor transistor_31 (.in(1'b1), .out(Y1), .gate(transistor_6_out));
  Transistor #(.\type ("n")) transistor_32 (.in(1'b0), .out(Y1), .gate(transistor_6_out));
  Transistor transistor_33 (.in(1'b1), .out(Y2), .gate(transistor_16_out));
  Transistor #(.\type ("n")) transistor_34 (.in(1'b0), .out(Y2), .gate(transistor_16_out));
  Transistor transistor_35 (.in(1'b1), .out(Y3), .gate(transistor_21_out));
  Transistor #(.\type ("n")) transistor_36 (.in(1'b0), .out(Y3), .gate(transistor_21_out));
endmodule

module decoder416 (
  input  A0,
  input  A1,
  input  A2,
  input  A3,
  output out_5,
  output out_6,
  output out_7,
  output out_8,
  output out_9,
  output out_10,
  output out_11,
  output out_12,
  output out_13,
  output out_14,
  output out_15,
  output out_16,
  output out_17,
  output out_18,
  output out_19,
  output out_20
);

  wire decoder24_1_y0, decoder24_1_y1, decoder24_1_y2, decoder24_1_y3;

  decoder24 decoder24_1 (
    ._1(A2), ._2(A3), .en(1'b1), .Y0(decoder24_1_y0), .Y1(decoder24_1_y1), .Y2(decoder24_1_y2),
    .Y3(decoder24_1_y3));
  decoder24 decoder24_2 (._1(A0), ._2(A1), .en(decoder24_1_y0), .Y0(out_5), .Y1(out_6), .Y2(out_7), .Y3(out_8));
  decoder24 decoder24_3 (._1(A0), ._2(A1), .en(decoder24_1_y1), .Y0(out_9), .Y1(out_10), .Y2(out_11), .Y3(out_12));
  decoder24 decoder24_4 (._1(A0), ._2(A1), .en(decoder24_1_y2), .Y0(out_13), .Y1(out_14), .Y2(out_15), .Y3(out_16));
  decoder24 decoder24_5 (._1(A0), ._2(A1), .en(decoder24_1_y3), .Y0(out_17), .Y1(out_18), .Y2(out_19), .Y3(out_20));
endmodule

module seg7 (
  input  in_1,
  input  in_2,
  input  in_3,
  input  in_4
);

  wire A_out, B_out, C_out, D_out, decoder416_1_out_5, decoder416_1_out_6, decoder416_1_out_7,
       decoder416_1_out_8, decoder416_1_out_9, decoder416_1_out_10, decoder416_1_out_11, decoder416_1_out_12,
       decoder416_1_out_13, decoder416_1_out_14, decoder416_1_out_15, decoder416_1_out_16,
       decoder416_1_out_17, decoder416_1_out_18, decoder416_1_out_19, decoder416_1_out_20, E_out, F_out,
       G_out, or_1_out;

  decoder416 decoder416_1 (
    .A0(in_1), .A1(in_2), .A2(in_3), .A3(in_4), .out_5(decoder416_1_out_5), .out_6(decoder416_1_out_6),
    .out_7(decoder416_1_out_7), .out_8(decoder416_1_out_8), .out_9(decoder416_1_out_9),
    .out_10(decoder416_1_out_10), .out_11(decoder416_1_out_11), .out_12(decoder416_1_out_12),
    .out_13(decoder416_1_out_13), .out_14(decoder416_1_out_14), .out_15(decoder416_1_out_15),
    .out_16(decoder416_1_out_16), .out_17(decoder416_1_out_17), .out_18(decoder416_1_out_18),
    .out_19(decoder416_1_out_19), .out_20(decoder416_1_out_20));
  or or_1 (or_1_out, decoder416_1_out_15, decoder416_1_out_16, decoder416_1_out_17, decoder416_1_out_18, decoder416_1_out_19, decoder416_1_out_20);
  or D (D_out, decoder416_1_out_5, decoder416_1_out_7, decoder416_1_out_8, decoder416_1_out_10, decoder416_1_out_11, decoder416_1_out_13, decoder416_1_out_14);
  or E (E_out, decoder416_1_out_5, decoder416_1_out_7, decoder416_1_out_11, decoder416_1_out_13);
  or F (F_out, decoder416_1_out_5, decoder416_1_out_9, decoder416_1_out_10, decoder416_1_out_11, decoder416_1_out_13, decoder416_1_out_14);
  or G (G_out, decoder416_1_out_7, decoder416_1_out_8, decoder416_1_out_9, decoder416_1_out_10, decoder416_1_out_11, decoder416_1_out_13, decoder416_1_out_14);
  or B (B_out, decoder416_1_out_5, decoder416_1_out_6, decoder416_1_out_7, decoder416_1_out_8, decoder416_1_out_9, decoder416_1_out_12, decoder416_1_out_13, decoder416_1_out_14);
  or A (A_out, decoder416_1_out_5, decoder416_1_out_7, decoder416_1_out_8, decoder416_1_out_10, decoder416_1_out_11, decoder416_1_out_12, decoder416_1_out_13, decoder416_1_out_14);
  or C (C_out, decoder416_1_out_5, decoder416_1_out_6, decoder416_1_out_8, decoder416_1_out_9, decoder416_1_out_10, decoder416_1_out_11, decoder416_1_out_12, decoder416_1_out_13, decoder416_1_out_14);
  _7_Segment_Display u_7_segment_display_1 (
    .g(G_out), .f(F_out), .a(A_out), .b(B_out), .e(E_out), .d(D_out), .c(C_out), .dp(or_1_out));
endmodule

module encoder164 (
  input  A0,
  input  A1,
  input  A2,
  input  A3,
  input  A4,
  input  A5,
  input  A6,
  input  A7,
  input  A8,
  input  A9,
  input  A10,
  input  A11,
  input  A12,
  input  A13,
  input  A14,
  input  A15,
  output out_17,
  output out_18,
  output out_19,
  output out_20
);

  or Y0 (out_17, A1, A3, A5, A7, A9, A11, A13, A15);
  or Y1 (out_18, A2, A3, A6, A7, A10, A11, A14, A15);
  or Y2 (out_19, A4, A5, A6, A7, A12, A13, A14, A15);
  or Y3 (out_20, A8, A9, A10, A11, A12, A13, A14, A15);
endmodule

module encoder164p (
  input  A15,
  input  A14,
  input  A13,
  input  A12,
  input  A11,
  input  A10,
  input  A9,
  input  A8,
  input  A7,
  input  A6,
  input  A5,
  input  A4,
  input  A3,
  input  A2,
  input  A1,
  input  A0,
  output Y0,
  output Y1,
  output Y2,
  output Y3
);

  wire and_1_out, and_2_out, and_3_out, and_4_out, and_5_out, and_6_out, and_7_out, and_8_out, and_9_out,
       and_10_out, and_11_out, and_12_out, and_13_out, and_14_out, and_15_out, and_16_out, and_17_out,
       and_18_out, and_19_out, and_20_out, and_21_out, and_22_out, and_23_out, and_24_out, and_25_out,
       and_26_out, and_28_out, not_1_out, not_2_out, not_3_out, not_4_out, not_5_out, not_6_out, not_7_out,
       not_8_out, not_9_out, not_10_out, not_11_out, not_12_out, not_13_out, not_14_out, not_15_out;

  not not_1 (not_1_out, A15);
  not not_2 (not_2_out, A14);
  not not_3 (not_3_out, A13);
  not not_4 (not_4_out, A12);
  not not_5 (not_5_out, A11);
  not not_6 (not_6_out, A10);
  not not_7 (not_7_out, A9);
  not not_8 (not_8_out, A8);
  not not_9 (not_9_out, A7);
  not not_10 (not_10_out, A6);
  not not_11 (not_11_out, A5);
  not not_12 (not_12_out, A4);
  not not_13 (not_13_out, A3);
  not not_14 (not_14_out, A2);
  not not_15 (not_15_out, A1);
  and and_1 (and_1_out, not_1_out, not_2_out);
  and and_2 (and_2_out, not_1_out, A14);
  and and_3 (and_3_out, and_1_out, not_3_out);
  and and_4 (and_4_out, and_1_out, A13);
  and and_5 (and_5_out, and_3_out, not_4_out);
  and and_6 (and_6_out, and_3_out, A12);
  and and_7 (and_7_out, and_5_out, not_5_out);
  and and_8 (and_8_out, and_5_out, A11);
  and and_9 (and_9_out, and_7_out, not_6_out);
  and and_10 (and_10_out, and_7_out, A10);
  and and_11 (and_11_out, and_9_out, not_7_out);
  and and_12 (and_12_out, and_9_out, A9);
  and and_13 (and_13_out, and_11_out, not_8_out);
  and and_14 (and_14_out, and_11_out, A8);
  and and_15 (and_15_out, and_13_out, not_9_out);
  and and_16 (and_16_out, and_13_out, A7);
  and and_17 (and_17_out, and_15_out, not_10_out);
  and and_18 (and_18_out, and_15_out, A6);
  and and_19 (and_19_out, and_17_out, not_11_out);
  and and_20 (and_20_out, and_17_out, A5);
  and and_21 (and_21_out, and_19_out, not_12_out);
  and and_22 (and_22_out, and_19_out, A4);
  and and_23 (and_23_out, and_21_out, not_13_out);
  and and_24 (and_24_out, and_21_out, A3);
  and and_25 (and_25_out, and_23_out, not_14_out);
  and and_26 (and_26_out, and_23_out, A2);
  // AND_Gate and_27 has open pins: in0=and_25_out, in1=not_15_out, out=open
  and and_28 (and_28_out, and_25_out, A1);
  or u_Y0 (Y0, and_28_out, and_24_out, and_20_out, and_16_out, and_12_out, and_8_out, and_4_out, A15);
  or u_Y1 (Y1, and_26_out, and_24_out, and_18_out, and_16_out, and_10_out, and_8_out, and_2_out, A15);
  or u_Y2 (Y2, and_22_out, and_20_out, and_18_out, and_16_out, and_6_out, and_4_out, and_2_out, A15);
  or u_Y3 (Y3, and_14_out, and_12_out, and_10_out, and_8_out, and_6_out, and_4_out, and_2_out, A15);
endmodule

module Multiplexer121 (
  input  in_1,
  input  in_2,
  input  in_3,
  output out_4
);

  wire and_1_out, and_2_out, decoder12_1_out_2, decoder12_1_out_3;

  decoder12 decoder12_1 (.in_1(in_2), .out_2(decoder12_1_out_2), .out_3(decoder12_1_out_3));
  and and_1 (and_1_out, in_1, decoder12_1_out_2);
  and and_2 (and_2_out, decoder12_1_out_3, in_3);
  or or_1 (out_4, and_1_out, and_2_out);
endmodule

module decoder12 (
  input  in_1,
  output out_2,
  output out_3
);

  Transistor transistor_1 (.in(1'b1), .out(out_2), .gate(in_1));
  Transistor #(.\type ("n")) transistor_2 (.in(1'b0), .out(out_2), .gate(in_1));

  assign out_3 = in_1;
endmodule

module Multiplexer341 (
  input  in_1,
  input  in_2,
  input  in_3,
  input  in_4,
  input  in_5,
  input  in_6,
  input  in_7,
  input  in_8,
  input  in_9,
  input  in_10,
  input  in_11,
  input  in_12,
  input  in_13,
  input  in_14,
  output out_15,
  output out_16,
  output out_17
);

  wire and_1_out, and_2_out, and_3_out, and_4_out, and_5_out, and_6_out, and_7_out, and_8_out, and_9_out,
       and_10_out, and_11_out, and_12_out, decoder24_1_y0, decoder24_1_y1, decoder24_1_y2, decoder24_1_y3,
       decoder24_2_y0, decoder24_2_y1, decoder24_2_y2, decoder24_2_y3, decoder24_3_y0, decoder24_3_y1,
       decoder24_3_y2, decoder24_3_y3;

  decoder24 decoder24_1 (
    ._1(in_6), ._2(in_8), .en(1'b1), .Y0(decoder24_1_y0), .Y1(decoder24_1_y1), .Y2(decoder24_1_y2),
    .Y3(decoder24_1_y3));
  decoder24 decoder24_2 (
    ._1(in_6), ._2(in_8), .en(1'b1), .Y0(decoder24_2_y0), .Y1(decoder24_2_y1), .Y2(decoder24_2_y2),
    .Y3(decoder24_2_y3));
  decoder24 decoder24_3 (
    ._1(in_6), ._2(in_8), .en(1'b1), .Y0(decoder24_3_y0), .Y1(decoder24_3_y1), .Y2(decoder24_3_y2),
    .Y3(decoder24_3_y3));
  and and_1 (and_1_out, decoder24_1_y0, in_1);
  and and_2 (and_2_out, decoder24_1_y1, in_2);
  and and_3 (and_3_out, in_3, decoder24_1_y2);
  and and_4 (and_4_out, in_4, decoder24_1_y3);
  and and_5 (and_5_out, decoder24_2_y0, in_5);
  and and_6 (and_6_out, decoder24_2_y1, in_7);
  and and_7 (and_7_out, in_9, decoder24_2_y2);
  and and_8 (and_8_out, in_10, decoder24_2_y3);
  and and_9 (and_9_out, decoder24_3_y0, in_11);
  and and_10 (and_10_out, decoder24_3_y1, in_12);
  and and_11 (and_11_out, in_13, decoder24_3_y2);
  and and_12 (and_12_out, in_14, decoder24_3_y3);
  or or_1 (out_15, and_1_out, and_2_out, and_3_out, and_4_out);
  or or_2 (out_16, and_5_out, and_6_out, and_7_out, and_8_out);
  or or_3 (out_17, and_9_out, and_10_out, and_11_out, and_12_out);
endmodule

module comparator4 (
  input  in_1,
  input  in_2,
  input  in_3,
  input  in_4,
  input  in_5,
  input  in_6,
  input  in_7,
  input  in_8
);

  wire and_1_out, xnor_1_out, xnor_2_out, xnor_3_out, xnor_4_out;

  xnor xnor_1 (xnor_1_out, in_1, in_2);
  xnor xnor_2 (xnor_2_out, in_3, in_4);
  xnor xnor_3 (xnor_3_out, in_5, in_6);
  xnor xnor_4 (xnor_4_out, in_7, in_8);
  and and_1 (and_1_out, xnor_1_out, xnor_2_out, xnor_3_out, xnor_4_out);
  LED led_1 (.in(and_1_out));
endmodule

module HalfAdder (
  input  in_1,
  input  in_2,
  output S,
  output Cout
);

  xor xor_1 (S, in_1, in_2);
  and and_1 (Cout, in_1, in_2);
endmodule

module FullAdder (
  input  in_1,
  input  in_2,
  input  Cin,
  output out_4,
  output Cout
);

  wire halfadder_1_cout, halfadder_1_s, halfadder_2_cout;

  HalfAdder halfadder_1 (.in_1(in_1), .in_2(in_2), .S(halfadder_1_s), .Cout(halfadder_1_cout));
  HalfAdder halfadder_2 (.in_1(halfadder_1_s), .in_2(Cin), .S(out_4), .Cout(halfadder_2_cout));
  or or_1 (Cout, halfadder_2_cout, halfadder_1_cout);
endmodule

module bitadder4seg7hex (
  input  in_1,
  input  in_2,
  input  in_3,
  input  in_4,
  input  in_5,
  input  in_6,
  input  in_7,
  input  in_8,
  input  in_9
);

  wire decoder416_1_out_5, decoder416_1_out_6, decoder416_1_out_7, decoder416_1_out_8, decoder416_1_out_9,
       decoder416_1_out_10, decoder416_1_out_11, decoder416_1_out_12, decoder416_1_out_13,
       decoder416_1_out_14, decoder416_1_out_15, decoder416_1_out_16, decoder416_1_out_17,
       decoder416_1_out_18, decoder416_1_out_19, decoder416_1_out_20, fulladder_1_cout, fulladder_1_out_4,
       fulladder_2_cout, fulladder_2_out_4, fulladder_3_cout, fulladder_3_out_4, fulladder_4_cout,
       fulladder_4_out_4, ha_1_out, ha_2_out, ha_out, hb_1_out, hb_2_out, hb_out, hc_1_out, hc_2_out, hc_out,
       hd_1_out, hd_2_out, hd_out, he_1_out, he_2_out, he_out, hf_1_out, hf_2_out, hf_out, hg_1_out,
       hg_2_out, hg_out;

  FullAdder fulladder_1 (.in_1(in_1), .in_2(in_5), .Cin(in_9), .out_4(fulladder_1_out_4), .Cout(fulladder_1_cout));
  FullAdder fulladder_2 (
    .in_1(in_2), .in_2(in_6), .Cin(fulladder_1_cout), .out_4(fulladder_2_out_4), .Cout(fulladder_2_cout));
  FullAdder fulladder_3 (
    .in_1(in_3), .in_2(in_7), .Cin(fulladder_2_cout), .out_4(fulladder_3_out_4), .Cout(fulladder_3_cout));
  FullAdder fulladder_4 (
    .in_1(in_4), .in_2(in_8), .Cin(fulladder_3_cout), .out_4(fulladder_4_out_4), .Cout(fulladder_4_cout));
  LED led_1 (.in(fulladder_4_cout));
  decoder416 decoder416_1 (
    .A0(fulladder_1_out_4), .A1(fulladder_2_out_4), .A2(fulladder_3_out_4), .A3(fulladder_4_out_4),
    .out_5(decoder416_1_out_5), .out_6(decoder416_1_out_6), .out_7(decoder416_1_out_7),
    .out_8(decoder416_1_out_8), .out_9(decoder416_1_out_9), .out_10(decoder416_1_out_10),
    .out_11(decoder416_1_out_11), .out_12(decoder416_1_out_12), .out_13(decoder416_1_out_13),
    .out_14(decoder416_1_out_14), .out_15(decoder416_1_out_15), .out_16(decoder416_1_out_16),
    .out_17(decoder416_1_out_17), .out_18(decoder416_1_out_18), .out_19(decoder416_1_out_19),
    .out_20(decoder416_1_out_20));
  or ha_1 (ha_1_out, decoder416_1_out_5, decoder416_1_out_7, decoder416_1_out_8, decoder416_1_out_10, decoder416_1_out_11, decoder416_1_out_12, decoder416_1_out_13, decoder416_1_out_14);
  or ha_2 (ha_2_out, decoder416_1_out_15, decoder416_1_out_17, decoder416_1_out_19, decoder416_1_out_20);
  or ha (ha_out, ha_1_out, ha_2_out);
  or hb_1 (hb_1_out, decoder416_1_out_5, decoder416_1_out_6, decoder416_1_out_7, decoder416_1_out_8, decoder416_1_out_9, decoder416_1_out_12, decoder416_1_out_13, decoder416_1_out_14);
  or hb_2 (hb_2_out, decoder416_1_out_15, decoder416_1_out_18, decoder416_1_out_15, decoder416_1_out_15);
  or hb (hb_out, hb_1_out, hb_2_out);
  or hc_1 (hc_1_out, decoder416_1_out_5, decoder416_1_out_6, decoder416_1_out_8, decoder416_1_out_9, decoder416_1_out_10, decoder416_1_out_11, decoder416_1_out_12, decoder416_1_out_13);
  or hc_2 (hc_2_out, decoder416_1_out_14, decoder416_1_out_15, decoder416_1_out_16, decoder416_1_out_18);
  or hc (hc_out, hc_1_out, hc_2_out);
  or hd_1 (hd_1_out, decoder416_1_out_5, decoder416_1_out_7, decoder416_1_out_8, decoder416_1_out_10, decoder416_1_out_11, decoder416_1_out_13, decoder416_1_out_14, decoder416_1_out_16);
  or hd_2 (hd_2_out, decoder416_1_out_17, decoder416_1_out_18, decoder416_1_out_19, decoder416_1_out_17);
  or hd (hd_out, hd_1_out, hd_2_out);
  or he_1 (he_1_out, decoder416_1_out_5, decoder416_1_out_7, decoder416_1_out_11, decoder416_1_out_13, decoder416_1_out_15, decoder416_1_out_16, decoder416_1_out_17, decoder416_1_out_18);
  or he_2 (he_2_out, decoder416_1_out_19, decoder416_1_out_20, decoder416_1_out_19, decoder416_1_out_19);
  or he (he_out, he_1_out, he_2_out);
  or hf_1 (hf_1_out, decoder416_1_out_5, decoder416_1_out_9, decoder416_1_out_10, decoder416_1_out_11, decoder416_1_out_13, decoder416_1_out_14, decoder416_1_out_15, decoder416_1_out_16);
  or hf_2 (hf_2_out, decoder416_1_out_17, decoder416_1_out_19, decoder416_1_out_20, decoder416_1_out_17);
  or hf (hf_out, hf_1_out, hf_2_out);
  or hg_1 (hg_1_out, decoder416_1_out_7, decoder416_1_out_8, decoder416_1_out_9, decoder416_1_out_10, decoder416_1_out_11, decoder416_1_out_13, decoder416_1_out_14, decoder416_1_out_15);
  or hg_2 (hg_2_out, decoder416_1_out_16, decoder416_1_out_18, decoder416_1_out_19, decoder416_1_out_20);
  or hg (hg_out, hg_1_out, hg_2_out);
  _7_Segment_Display u_7_segment_display_1 (
    .g(hg_out), .f(hf_out), .a(ha_out), .b(hb_out), .e(he_out), .d(hd_out), .c(hc_out), .dp(1'b0));
endmodule

module seg7switch (
  input  A0,
  input  A1,
  input  A2,
  input  A3,
  input  S
);

  wire and_1_out, and_2_out, and_3_out, and_4_out, and_5_out, and_6_out, and_7_out, dec_a_out, dec_b_out,
       dec_c1_out, dec_c2_out, dec_d_out, dec_e_out, dec_f_out, dec_g_out, decoder416_1_out_5,
       decoder416_1_out_6, decoder416_1_out_7, decoder416_1_out_8, decoder416_1_out_9, decoder416_1_out_10,
       decoder416_1_out_11, decoder416_1_out_12, decoder416_1_out_13, decoder416_1_out_14,
       decoder416_1_out_15, decoder416_1_out_16, decoder416_1_out_17, decoder416_1_out_18,
       decoder416_1_out_19, decoder416_1_out_20, dp_out, hex_a_out, hex_b_out, hex_c_out, hex_d_out,
       hex_e_out, hex_f_out, hex_g_out, mrg_a_out, mrg_b_out, mrg_c_out, mrg_d_out, mrg_e_out, mrg_f_out,
       mrg_g_out;

  decoder416 decoder416_1 (
    .A0(A0), .A1(A1), .A2(A2), .A3(A3), .out_5(decoder416_1_out_5), .out_6(decoder416_1_out_6),
    .out_7(decoder416_1_out_7), .out_8(decoder416_1_out_8), .out_9(decoder416_1_out_9),
    .out_10(decoder416_1_out_10), .out_11(decoder416_1_out_11), .out_12(decoder416_1_out_12),
    .out_13(decoder416_1_out_13), .out_14(decoder416_1_out_14), .out_15(decoder416_1_out_15),
    .out_16(decoder416_1_out_16), .out_17(decoder416_1_out_17), .out_18(decoder416_1_out_18),
    .out_19(decoder416_1_out_19), .out_20(decoder416_1_out_20));
  and and_1 (and_1_out, S, decoder416_1_out_15);
  and and_2 (and_2_out, S, decoder416_1_out_16);
  and and_3 (and_3_out, S, decoder416_1_out_17);
  and and_4 (and_4_out, S, decoder416_1_out_18);
  and and_5 (and_5_out, S, decoder416_1_out_19);
  and and_6 (and_6_out, S, decoder416_1_out_20);
  or dec_a (dec_a_out, decoder416_1_out_5, decoder416_1_out_7, decoder416_1_out_8, decoder416_1_out_10, decoder416_1_out_11, decoder416_1_out_12, decoder416_1_out_13, decoder416_1_out_14);
  or dec_b (dec_b_out, decoder416_1_out_5, decoder416_1_out_6, decoder416_1_out_7, decoder416_1_out_8, decoder416_1_out_9, decoder416_1_out_12, decoder416_1_out_13, decoder416_1_out_14);
  or dec_c1 (dec_c1_out, decoder416_1_out_5, decoder416_1_out_6, decoder416_1_out_8, decoder416_1_out_9, decoder416_1_out_10, decoder416_1_out_11, decoder416_1_out_12, decoder416_1_out_13);
  or dec_d (dec_d_out, decoder416_1_out_5, decoder416_1_out_7, decoder416_1_out_8, decoder416_1_out_10, decoder416_1_out_11, decoder416_1_out_13, decoder416_1_out_14, decoder416_1_out_5);
  or dec_e (dec_e_out, decoder416_1_out_5, decoder416_1_out_7, decoder416_1_out_11, decoder416_1_out_13);
  or dec_f (dec_f_out, decoder416_1_out_5, decoder416_1_out_9, decoder416_1_out_10, decoder416_1_out_11, decoder416_1_out_13, decoder416_1_out_14);
  or dec_g (dec_g_out, decoder416_1_out_7, decoder416_1_out_8, decoder416_1_out_9, decoder416_1_out_10, decoder416_1_out_11, decoder416_1_out_13, decoder416_1_out_14, decoder416_1_out_7);
  or dp (dp_out, decoder416_1_out_15, decoder416_1_out_16, decoder416_1_out_17, decoder416_1_out_18, decoder416_1_out_19, decoder416_1_out_20);
  or dec_c2 (dec_c2_out, dec_c1_out, decoder416_1_out_14, dec_c1_out, dec_c1_out);
  or hex_a (hex_a_out, and_1_out, and_3_out, and_5_out, and_6_out);
  or hex_b (hex_b_out, and_1_out, and_4_out, and_1_out, and_1_out);
  or hex_c (hex_c_out, and_1_out, and_2_out, and_4_out, and_1_out);
  or hex_d (hex_d_out, and_2_out, and_3_out, and_4_out, and_5_out);
  or hex_e (hex_e_out, and_1_out, and_2_out, and_3_out, and_4_out, and_5_out, and_6_out);
  or hex_f (hex_f_out, and_1_out, and_2_out, and_3_out, and_5_out, and_6_out, and_1_out);
  or hex_g (hex_g_out, and_1_out, and_2_out, and_4_out, and_5_out, and_6_out, and_1_out);
  or mrg_a (mrg_a_out, dec_a_out, hex_a_out, dec_a_out, dec_a_out);
  or mrg_b (mrg_b_out, dec_b_out, hex_b_out, dec_b_out, dec_b_out);
  or mrg_c (mrg_c_out, dec_c2_out, hex_c_out, dec_c2_out, dec_c2_out);
  or mrg_d (mrg_d_out, dec_d_out, hex_d_out, dec_d_out, dec_d_out);
  or mrg_e (mrg_e_out, dec_e_out, hex_e_out, dec_e_out, dec_e_out);
  or mrg_f (mrg_f_out, dec_f_out, hex_f_out, dec_f_out, dec_f_out);
  or mrg_g (mrg_g_out, dec_g_out, hex_g_out, dec_g_out, dec_g_out);
  not not_1 (dp_out, S);
  and and_7 (and_7_out, dp_out, dp_out);
  _7_Segment_Display u_7_segment_display_1 (
    .g(mrg_g_out), .f(mrg_f_out), .a(mrg_a_out), .b(mrg_b_out), .e(mrg_e_out), .d(mrg_d_out), .c(mrg_c_out),
    .dp(and_7_out));
endmodule

module seg7hex (
  input  A0,
  input  A1,
  input  A2,
  input  A3
);

  wire decoder416_1_out_5, decoder416_1_out_6, decoder416_1_out_7, decoder416_1_out_8, decoder416_1_out_9,
       decoder416_1_out_10, decoder416_1_out_11, decoder416_1_out_12, decoder416_1_out_13,
       decoder416_1_out_14, decoder416_1_out_15, decoder416_1_out_16, decoder416_1_out_17,
       decoder416_1_out_18, decoder416_1_out_19, decoder416_1_out_20, ha_1_out, ha_2_out, ha_out, hb_1_out,
       hb_2_out, hb_out, hc_1_out, hc_2_out, hc_out, hd_1_out, hd_2_out, hd_out, he_1_out, he_2_out, he_out,
       hf_1_out, hf_2_out, hf_out, hg_1_out, hg_2_out, hg_out;

  decoder416 decoder416_1 (
    .A0(A0), .A1(A1), .A2(A2), .A3(A3), .out_5(decoder416_1_out_5), .out_6(decoder416_1_out_6),
    .out_7(decoder416_1_out_7), .out_8(decoder416_1_out_8), .out_9(decoder416_1_out_9),
    .out_10(decoder416_1_out_10), .out_11(decoder416_1_out_11), .out_12(decoder416_1_out_12),
    .out_13(decoder416_1_out_13), .out_14(decoder416_1_out_14), .out_15(decoder416_1_out_15),
    .out_16(decoder416_1_out_16), .out_17(decoder416_1_out_17), .out_18(decoder416_1_out_18),
    .out_19(decoder416_1_out_19), .out_20(decoder416_1_out_20));
  or ha_1 (ha_1_out, decoder416_1_out_5, decoder416_1_out_7, decoder416_1_out_8, decoder416_1_out_10, decoder416_1_out_11, decoder416_1_out_12, decoder416_1_out_13, decoder416_1_out_14);
  or ha_2 (ha_2_out, decoder416_1_out_15, decoder416_1_out_17, decoder416_1_out_19, decoder416_1_out_20);
  or ha (ha_out, ha_1_out, ha_2_out);
  or hb_1 (hb_1_out, decoder416_1_out_5, decoder416_1_out_6, decoder416_1_out_7, decoder416_1_out_8, decoder416_1_out_9, decoder416_1_out_12, decoder416_1_out_13, decoder416_1_out_14);
  or hb_2 (hb_2_out, decoder416_1_out_15, decoder416_1_out_18, decoder416_1_out_15, decoder416_1_out_15);
  or hb (hb_out, hb_1_out, hb_2_out);
  or hc_1 (hc_1_out, decoder416_1_out_5, decoder416_1_out_6, decoder416_1_out_8, decoder416_1_out_9, decoder416_1_out_10, decoder416_1_out_11, decoder416_1_out_12, decoder416_1_out_13);
  or hc_2 (hc_2_out, decoder416_1_out_14, decoder416_1_out_15, decoder416_1_out_16, decoder416_1_out_18);
  or hc (hc_out, hc_1_out, hc_2_out);
  or hd_1 (hd_1_out, decoder416_1_out_5, decoder416_1_out_7, decoder416_1_out_8, decoder416_1_out_10, decoder416_1_out_11, decoder416_1_out_13, decoder416_1_out_14, decoder416_1_out_16);
  or hd_2 (hd_2_out, decoder416_1_out_17, decoder416_1_out_18, decoder416_1_out_19, decoder416_1_out_17);
  or hd (hd_out, hd_1_out, hd_2_out);
  or he_1 (he_1_out, decoder416_1_out_5, decoder416_1_out_7, decoder416_1_out_11, decoder416_1_out_13, decoder416_1_out_15, decoder416_1_out_16, decoder416_1_out_17, decoder416_1_out_18);
  or he_2 (he_2_out, decoder416_1_out_19, decoder416_1_out_20, decoder416_1_out_19, decoder416_1_out_19);
  or he (he_out, he_1_out, he_2_out);
  or hf_1 (hf_1_out, decoder416_1_out_5, decoder416_1_out_9, decoder416_1_out_10, decoder416_1_out_11, decoder416_1_out_13, decoder416_1_out_14, decoder416_1_out_15, decoder416_1_out_16);
  or hf_2 (hf_2_out, decoder416_1_out_17, decoder416_1_out_19, decoder416_1_out_20, decoder416_1_out_17);
  or hf (hf_out, hf_1_out, hf_2_out);
  or hg_1 (hg_1_out, decoder416_1_out_7, decoder416_1_out_8, decoder416_1_out_9, decoder416_1_out_10, decoder416_1_out_11, decoder416_1_out_13, decoder416_1_out_14, decoder416_1_out_15);
  or hg_2 (hg_2_out, decoder416_1_out_16, decoder416_1_out_18, decoder416_1_out_19, decoder416_1_out_20);
  or hg (hg_out, hg_1_out, hg_2_out);
  _7_Segment_Display u_7_segment_display_1 (
    .g(hg_out), .f(hf_out), .a(ha_out), .b(hb_out), .e(he_out), .d(hd_out), .c(hc_out), .dp(1'b0));
endmodule

module XOR (
  input  x,
  input  y,
  output o
);

  wire And1_out, And2_out, not_1_out, not_2_out;

  not not_1 (not_1_out, y);
  not not_2 (not_2_out, x);
  and And1 (And1_out, x, not_1_out);
  and And2 (And2_out, not_2_out, y);
  or or1 (o, And1_out, And2_out);

  // Notes on the sheet:
  //   XOR
endmodule

module NOR2 (
  input  in_1,
  input  in_2,
  output out_3
);

  wire transistor_1_out, transistor_2_out, transistor_3_out, transistor_6_out;

  Transistor transistor_1 (.in(1'b1), .out(transistor_1_out), .gate(in_1));
  Transistor transistor_2 (.in(transistor_1_out), .out(transistor_2_out), .gate(in_2));
  Transistor #(.\type ("n")) transistor_3 (.in(transistor_2_out), .out(transistor_3_out), .gate(in_1));
  Transistor #(.\type ("n")) transistor_4 (.in(transistor_2_out), .out(transistor_3_out), .gate(in_2));
  Transistor transistor_5 (.in(1'b1), .out(out_3), .gate(transistor_2_out));
  Transistor #(.\type ("n")) transistor_6 (.in(out_3), .out(transistor_6_out), .gate(transistor_2_out));
  // also tied to GND on the sheet: {transistor_3_out, transistor_6_out}
endmodule

module subtractor4bitseg7hex (
  input  in_1,
  input  in_2,
  input  in_3,
  input  in_4,
  input  in_5,
  input  in_6,
  input  in_7,
  input  in_8
);

  wire decoder416_1_out_5, decoder416_1_out_6, decoder416_1_out_7, decoder416_1_out_8, decoder416_1_out_9,
       decoder416_1_out_10, decoder416_1_out_11, decoder416_1_out_12, decoder416_1_out_13,
       decoder416_1_out_14, decoder416_1_out_15, decoder416_1_out_16, decoder416_1_out_17,
       decoder416_1_out_18, decoder416_1_out_19, decoder416_1_out_20, fulladder_1_cout, fulladder_1_out_4,
       fulladder_2_cout, fulladder_2_out_4, fulladder_3_cout, fulladder_3_out_4, fulladder_4_cout,
       fulladder_4_out_4, ha_1_out, ha_2_out, ha_out, hb_1_out, hb_2_out, hb_out, hc_1_out, hc_2_out, hc_out,
       hd_1_out, hd_2_out, hd_out, he_1_out, he_2_out, he_out, hf_1_out, hf_2_out, hf_out, hg_1_out,
       hg_2_out, hg_out, not_1_out, not_2_out, not_3_out, not_4_out;

  not not_1 (not_1_out, in_5);
  FullAdder fulladder_1 (.in_1(in_1), .in_2(not_1_out), .Cin(1'b1), .out_4(fulladder_1_out_4), .Cout(fulladder_1_cout));
  not not_2 (not_2_out, in_6);
  FullAdder fulladder_2 (
    .in_1(in_2), .in_2(not_2_out), .Cin(fulladder_1_cout), .out_4(fulladder_2_out_4), .Cout(fulladder_2_cout));
  not not_3 (not_3_out, in_7);
  FullAdder fulladder_3 (
    .in_1(in_3), .in_2(not_3_out), .Cin(fulladder_2_cout), .out_4(fulladder_3_out_4), .Cout(fulladder_3_cout));
  not not_4 (not_4_out, in_8);
  FullAdder fulladder_4 (
    .in_1(in_4), .in_2(not_4_out), .Cin(fulladder_3_cout), .out_4(fulladder_4_out_4), .Cout(fulladder_4_cout));
  LED led_1 (.in(fulladder_4_cout));
  decoder416 decoder416_1 (
    .A0(fulladder_1_out_4), .A1(fulladder_2_out_4), .A2(fulladder_3_out_4), .A3(fulladder_4_out_4),
    .out_5(decoder416_1_out_5), .out_6(decoder416_1_out_6), .out_7(decoder416_1_out_7),
    .out_8(decoder416_1_out_8), .out_9(decoder416_1_out_9), .out_10(decoder416_1_out_10),
    .out_11(decoder416_1_out_11), .out_12(decoder416_1_out_12), .out_13(decoder416_1_out_13),
    .out_14(decoder416_1_out_14), .out_15(decoder416_1_out_15), .out_16(decoder416_1_out_16),
    .out_17(decoder416_1_out_17), .out_18(decoder416_1_out_18), .out_19(decoder416_1_out_19),
    .out_20(decoder416_1_out_20));
  or ha_1 (ha_1_out, decoder416_1_out_5, decoder416_1_out_7, decoder416_1_out_8, decoder416_1_out_10, decoder416_1_out_11, decoder416_1_out_12, decoder416_1_out_13, decoder416_1_out_14);
  or ha_2 (ha_2_out, decoder416_1_out_15, decoder416_1_out_17, decoder416_1_out_19, decoder416_1_out_20);
  or ha (ha_out, ha_1_out, ha_2_out);
  or hb_1 (hb_1_out, decoder416_1_out_5, decoder416_1_out_6, decoder416_1_out_7, decoder416_1_out_8, decoder416_1_out_9, decoder416_1_out_12, decoder416_1_out_13, decoder416_1_out_14);
  or hb_2 (hb_2_out, decoder416_1_out_15, decoder416_1_out_18, decoder416_1_out_15, decoder416_1_out_15);
  or hb (hb_out, hb_1_out, hb_2_out);
  or hc_1 (hc_1_out, decoder416_1_out_5, decoder416_1_out_6, decoder416_1_out_8, decoder416_1_out_9, decoder416_1_out_10, decoder416_1_out_11, decoder416_1_out_12, decoder416_1_out_13);
  or hc_2 (hc_2_out, decoder416_1_out_14, decoder416_1_out_15, decoder416_1_out_16, decoder416_1_out_18);
  or hc (hc_out, hc_1_out, hc_2_out);
  or hd_1 (hd_1_out, decoder416_1_out_5, decoder416_1_out_7, decoder416_1_out_8, decoder416_1_out_10, decoder416_1_out_11, decoder416_1_out_13, decoder416_1_out_14, decoder416_1_out_16);
  or hd_2 (hd_2_out, decoder416_1_out_17, decoder416_1_out_18, decoder416_1_out_19, decoder416_1_out_17);
  or hd (hd_out, hd_1_out, hd_2_out);
  or he_1 (he_1_out, decoder416_1_out_5, decoder416_1_out_7, decoder416_1_out_11, decoder416_1_out_13, decoder416_1_out_15, decoder416_1_out_16, decoder416_1_out_17, decoder416_1_out_18);
  or he_2 (he_2_out, decoder416_1_out_19, decoder416_1_out_20, decoder416_1_out_19, decoder416_1_out_19);
  or he (he_out, he_1_out, he_2_out);
  or hf_1 (hf_1_out, decoder416_1_out_5, decoder416_1_out_9, decoder416_1_out_10, decoder416_1_out_11, decoder416_1_out_13, decoder416_1_out_14, decoder416_1_out_15, decoder416_1_out_16);
  or hf_2 (hf_2_out, decoder416_1_out_17, decoder416_1_out_19, decoder416_1_out_20, decoder416_1_out_17);
  or hf (hf_out, hf_1_out, hf_2_out);
  or hg_1 (hg_1_out, decoder416_1_out_7, decoder416_1_out_8, decoder416_1_out_9, decoder416_1_out_10, decoder416_1_out_11, decoder416_1_out_13, decoder416_1_out_14, decoder416_1_out_15);
  or hg_2 (hg_2_out, decoder416_1_out_16, decoder416_1_out_18, decoder416_1_out_19, decoder416_1_out_20);
  or hg (hg_out, hg_1_out, hg_2_out);
  _7_Segment_Display u_7_segment_display_1 (
    .g(hg_out), .f(hf_out), .a(ha_out), .b(hb_out), .e(he_out), .d(hd_out), .c(hc_out), .dp(1'b0));
endmodule

module YuanMaAdder4bit (
  input  A,
  input  B,
  input  in_3,
  input  in_4,
  input  in_5,
  input  in_6,
  input  in_7,
  input  in_8,
  input  in_9
);

  wire and_1_out, decoder416_1_out_5, decoder416_1_out_6, decoder416_1_out_7, decoder416_1_out_8,
       decoder416_1_out_9, decoder416_1_out_10, decoder416_1_out_11, decoder416_1_out_12,
       decoder416_1_out_13, decoder416_1_out_14, decoder416_1_out_15, decoder416_1_out_16,
       decoder416_1_out_17, decoder416_1_out_18, decoder416_1_out_19, decoder416_1_out_20, fulladder_1_cout,
       fulladder_1_out_4, fulladder_2_cout, fulladder_2_out_4, fulladder_3_cout, fulladder_3_out_4,
       fulladder_4_cout, fulladder_4_out_4, fulladder_5_cout, fulladder_5_out_4, fulladder_6_cout,
       fulladder_6_out_4, fulladder_7_cout, fulladder_7_out_4, fulladder_8_cout, fulladder_8_out_4,
       fulladder_9_cout, fulladder_9_out_4, ha_1_out, ha_2_out, ha_out, hb_1_out, hb_2_out, hb_out, hc_1_out,
       hc_2_out, hc_out, hd_1_out, hd_2_out, hd_out, he_1_out, he_2_out, he_out, hf_1_out, hf_2_out, hf_out,
       hg_1_out, hg_2_out, hg_out, multiplexer121_1_out_4, multiplexer121_2_out_4, multiplexer121_3_out_4,
       multiplexer121_4_out_4, multiplexer121_5_out_4, multiplexer121_6_out_4, multiplexer121_7_out_4,
       multiplexer121_8_out_4, not_1_out, not_2_out, not_3_out, not_4_out, not_5_out, not_6_out, not_7_out,
       xnor_1_out;

  not not_1 (not_1_out, in_4);
  not not_2 (not_2_out, in_8);
  FullAdder fulladder_1 (.in_1(in_8), .in_2(in_4), .Cin(in_9), .out_4(fulladder_1_out_4), .Cout(fulladder_1_cout));
  FullAdder fulladder_2 (.in_1(in_8), .in_2(not_1_out), .Cin(1'b1), .out_4(fulladder_2_out_4), .Cout(fulladder_2_cout));
  FullAdder fulladder_3 (.in_1(in_4), .in_2(not_2_out), .Cin(1'b1), .out_4(fulladder_3_out_4), .Cout(fulladder_3_cout));
  not not_3 (not_3_out, in_3);
  not not_4 (not_4_out, in_7);
  FullAdder fulladder_4 (
    .in_1(in_7), .in_2(in_3), .Cin(fulladder_1_cout), .out_4(fulladder_4_out_4), .Cout(fulladder_4_cout));
  FullAdder fulladder_5 (
    .in_1(in_7), .in_2(not_3_out), .Cin(fulladder_2_cout), .out_4(fulladder_5_out_4), .Cout(fulladder_5_cout));
  FullAdder fulladder_6 (
    .in_1(in_3), .in_2(not_4_out), .Cin(fulladder_3_cout), .out_4(fulladder_6_out_4), .Cout(fulladder_6_cout));
  xnor xnor_1 (xnor_1_out, A, in_5);
  not not_5 (not_5_out, B);
  not not_6 (not_6_out, in_6);
  FullAdder fulladder_7 (
    .in_1(in_6), .in_2(B), .Cin(fulladder_4_cout), .out_4(fulladder_7_out_4), .Cout(fulladder_7_cout));
  FullAdder fulladder_8 (
    .in_1(in_6), .in_2(not_5_out), .Cin(fulladder_5_cout), .out_4(fulladder_8_out_4), .Cout(fulladder_8_cout));
  FullAdder fulladder_9 (
    .in_1(B), .in_2(not_6_out), .Cin(fulladder_6_cout), .out_4(fulladder_9_out_4), .Cout(fulladder_9_cout));
  LED led_1 (.in(fulladder_9_cout));
  not not_7 (not_7_out, fulladder_8_cout);
  Multiplexer121 multiplexer121_1 (
    .in_1(fulladder_2_out_4), .in_2(not_7_out), .in_3(fulladder_3_out_4), .out_4(multiplexer121_1_out_4));
  Multiplexer121 multiplexer121_2 (
    .in_1(fulladder_5_out_4), .in_2(not_7_out), .in_3(fulladder_6_out_4), .out_4(multiplexer121_2_out_4));
  Multiplexer121 multiplexer121_3 (
    .in_1(fulladder_8_out_4), .in_2(not_7_out), .in_3(fulladder_9_out_4), .out_4(multiplexer121_3_out_4));
  decoder416 decoder416_1 (
    .A0(multiplexer121_4_out_4), .A1(multiplexer121_5_out_4), .A2(multiplexer121_6_out_4), .A3(1'b0),
    .out_5(decoder416_1_out_5), .out_6(decoder416_1_out_6), .out_7(decoder416_1_out_7),
    .out_8(decoder416_1_out_8), .out_9(decoder416_1_out_9), .out_10(decoder416_1_out_10),
    .out_11(decoder416_1_out_11), .out_12(decoder416_1_out_12), .out_13(decoder416_1_out_13),
    .out_14(decoder416_1_out_14), .out_15(decoder416_1_out_15), .out_16(decoder416_1_out_16),
    .out_17(decoder416_1_out_17), .out_18(decoder416_1_out_18), .out_19(decoder416_1_out_19),
    .out_20(decoder416_1_out_20));
  and and_1 (and_1_out, xnor_1_out, fulladder_7_cout);
  Multiplexer121 multiplexer121_4 (
    .in_1(multiplexer121_1_out_4), .in_2(xnor_1_out), .in_3(fulladder_1_out_4), .out_4(multiplexer121_4_out_4));
  Multiplexer121 multiplexer121_5 (
    .in_1(multiplexer121_2_out_4), .in_2(xnor_1_out), .in_3(fulladder_4_out_4), .out_4(multiplexer121_5_out_4));
  Multiplexer121 multiplexer121_6 (
    .in_1(multiplexer121_3_out_4), .in_2(xnor_1_out), .in_3(fulladder_7_out_4), .out_4(multiplexer121_6_out_4));
  LED led_2 (.in(and_1_out));
  Multiplexer121 multiplexer121_7 (.in_1(A), .in_2(fulladder_8_cout), .in_3(in_5), .out_4(multiplexer121_7_out_4));
  Multiplexer121 multiplexer121_8 (
    .in_1(multiplexer121_7_out_4), .in_2(xnor_1_out), .in_3(in_5), .out_4(multiplexer121_8_out_4));
  or ha_1 (ha_1_out, decoder416_1_out_5, decoder416_1_out_7, decoder416_1_out_8, decoder416_1_out_10, decoder416_1_out_11, decoder416_1_out_12, decoder416_1_out_13, decoder416_1_out_14);
  or ha_2 (ha_2_out, decoder416_1_out_15, decoder416_1_out_17, decoder416_1_out_19, decoder416_1_out_20);
  or ha (ha_out, ha_1_out, ha_2_out);
  or hb_1 (hb_1_out, decoder416_1_out_5, decoder416_1_out_6, decoder416_1_out_7, decoder416_1_out_8, decoder416_1_out_9, decoder416_1_out_12, decoder416_1_out_13, decoder416_1_out_14);
  or hb_2 (hb_2_out, decoder416_1_out_15, decoder416_1_out_18, decoder416_1_out_15, decoder416_1_out_15);
  or hb (hb_out, hb_1_out, hb_2_out);
  or hc_1 (hc_1_out, decoder416_1_out_5, decoder416_1_out_6, decoder416_1_out_8, decoder416_1_out_9, decoder416_1_out_10, decoder416_1_out_11, decoder416_1_out_12, decoder416_1_out_13);
  or hc_2 (hc_2_out, decoder416_1_out_14, decoder416_1_out_15, decoder416_1_out_16, decoder416_1_out_18);
  or hc (hc_out, hc_1_out, hc_2_out);
  or hd_1 (hd_1_out, decoder416_1_out_5, decoder416_1_out_7, decoder416_1_out_8, decoder416_1_out_10, decoder416_1_out_11, decoder416_1_out_13, decoder416_1_out_14, decoder416_1_out_16);
  or hd_2 (hd_2_out, decoder416_1_out_17, decoder416_1_out_18, decoder416_1_out_19, decoder416_1_out_17);
  or hd (hd_out, hd_1_out, hd_2_out);
  or he_1 (he_1_out, decoder416_1_out_5, decoder416_1_out_7, decoder416_1_out_11, decoder416_1_out_13, decoder416_1_out_15, decoder416_1_out_16, decoder416_1_out_17, decoder416_1_out_18);
  or he_2 (he_2_out, decoder416_1_out_19, decoder416_1_out_20, decoder416_1_out_19, decoder416_1_out_19);
  or he (he_out, he_1_out, he_2_out);
  or hf_1 (hf_1_out, decoder416_1_out_5, decoder416_1_out_9, decoder416_1_out_10, decoder416_1_out_11, decoder416_1_out_13, decoder416_1_out_14, decoder416_1_out_15, decoder416_1_out_16);
  or hf_2 (hf_2_out, decoder416_1_out_17, decoder416_1_out_19, decoder416_1_out_20, decoder416_1_out_17);
  or hf (hf_out, hf_1_out, hf_2_out);
  or hg_1 (hg_1_out, decoder416_1_out_7, decoder416_1_out_8, decoder416_1_out_9, decoder416_1_out_10, decoder416_1_out_11, decoder416_1_out_13, decoder416_1_out_14, decoder416_1_out_15);
  or hg_2 (hg_2_out, decoder416_1_out_16, decoder416_1_out_18, decoder416_1_out_19, decoder416_1_out_20);
  or hg (hg_out, hg_1_out, hg_2_out);
  _7_Segment_Display u_7_segment_display_1 (
    .g(multiplexer121_8_out_4), .f(1'b0), .a(1'b0), .b(1'b0), .e(1'b0), .d(1'b0), .c(1'b0), .dp(1'b0));
  _7_Segment_Display u_7_segment_display_2 (
    .g(hg_out), .f(hf_out), .a(ha_out), .b(hb_out), .e(he_out), .d(hd_out), .c(hc_out), .dp(1'b0));

  // Notes on the sheet:
  //   A+B
  //   A-B
  //   B-A
endmodule
